# Fritzing sketch DHT11-MQ135-Thingspeak_wiring (saved by Fritzing 0.9.4)
breadboards: 1

parts:
  ESP8266v3 = NodeMCU V3.0
  DHT11 = DHT11 Humitidy and Temperature Sensor
  R1 = Resistor [tolerance=±5% resistance=4.7k package=THT]
  MQ135 = MQ-135

nets:
  3V3: ESP8266v3.3V3, DHT11.VDD, R1.Pin_1
  GND: ESP8266v3.GND, DHT11.GND, MQ135.GND
  N1: ESP8266v3.RX, DHT11.DATA, R1.Pin_0
  N2: ESP8266v3.VU, MQ135.VCC
  N3: ESP8266v3.A0, MQ135.A0

custom parts:
  NodeMCU V3.0: ESP8266 based NodeMCU
  DHT11 Humitidy and Temperature Sensor: DHT11 Humidity and Temperature Sensor
