# Fritzing sketch DHT11-Thingspeak_wiring (saved by Fritzing 0.9.4)
breadboards: 1

parts:
  ESP8266v3 = NodeMCU V3.0
  DHT1 = DHT11 Humitidy and Temperature Sensor
  R1 = Resistor [tolerance=±5% resistance=4.7k package=THT]

nets:
  3V3: ESP8266v3.3V3, DHT1.VDD, R1.Pin_1
  N1: ESP8266v3.RX, DHT1.DATA, R1.Pin_0
  GND: ESP8266v3.GND, DHT1.GND

custom parts:
  NodeMCU V3.0: ESP8266 based NodeMCU
  DHT11 Humitidy and Temperature Sensor: DHT11 Humidity and Temperature Sensor
